# Fritzing sketch SmarThermo (saved by Fritzing 0.9.2b)
breadboards: 1

parts:
  Raspberry_Pi_Zero1 = Raspberry Pi Zero
  DS3 = DS18B20 1-Wire Temperature Sensor Probe Cable
  R1 = Resistor [tolerance=±5% resistance=4.7 package="0805 [SMD]"]

nets:
  3V3: Raspberry_Pi_Zero1.3v3, Raspberry_Pi_Zero1.3V3, DS3.VDD, R1.Pin_1
  N1: Raspberry_Pi_Zero1.GIPO4, DS3.DQ, R1.Pin_0
  GND: Raspberry_Pi_Zero1.GND, DS3.GND

notes:
  DS18B20
